// Logisim project ALU.circ as structural Verilog: 4 circuits, main circuit ALUcircuit
module ALUcircuit (
  input  [3:0] ALUsel,
  input  [31:0] A,
  input  [31:0] B,
  output [31:0] Result,
  output is_zero,
  output Overflow
);

  wire big_adder_1_overflow, comparator_1_lt, comparator_2_lt, comparator_4_eq;
  wire [31:0] and_1_out, big_adder_1_out_3, bit_extender_1_out, bit_extender_2_out, bit_extender_3_out,
       mulh_1_lower, multiplier_1_cout, multiplier_1_out, or_1_out, shifter_1_out, shifter_2_out,
       shifter_3_out, subtractor_1_out, xor_1_out;

  big_adder big_adder_1 (.A(A), .B(B), .out_3(big_adder_1_out_3), .Overflow(big_adder_1_overflow));  // open: COUT
  Shifter #(.width(32)) shifter_1 (.in(A), .\dist (B[4:0]), .out(shifter_1_out));
  Shifter #(.shift("lr"), .width(32)) shifter_2 (.in(A), .\dist (B[4:0]), .out(shifter_2_out));
  Comparator #(.mode("unsigned"), .width(32)) comparator_1 (.a(A), .b(B), .lt(comparator_1_lt));  // open: gt, eq
  Comparator #(.width(32)) comparator_2 (.a(A), .b(B), .lt(comparator_2_lt));  // open: gt, eq
  assign bit_extender_1_out = {{31{1'b0}}, comparator_1_lt};  // Bit_Extender bit_extender_1
  assign xor_1_out = A ^ B;  // XOR_Gate xor_1, 32 bits wide
  Subtractor #(.width(32)) subtractor_1 (.a(A), .b(B), .out(subtractor_1_out));  // open: bin, bout
  Multiplier #(.width(32)) multiplier_1 (.a(A), .b(B), .out(multiplier_1_out), .cout(multiplier_1_cout));  // open: cin
  assign bit_extender_2_out = {{31{1'b0}}, comparator_2_lt};  // Bit_Extender bit_extender_2
  assign or_1_out = A | B;  // OR_Gate or_1, 32 bits wide
  assign and_1_out = A & B;  // AND_Gate and_1, 32 bits wide
  MULh mulh_1 (.NUM1(A), .in_2(1'b0), .NUM2(B), .LOWER(mulh_1_lower));  // open: HIgher
  Shifter #(.shift("ar"), .width(32)) shifter_3 (.in(A), .\dist (B[4:0]), .out(shifter_3_out));
  Multiplexer #(.enable("true"), .select(4), .width(32)) multiplexer_1 (
    .in0(big_adder_1_out_3), .in1(shifter_1_out), .in2(bit_extender_2_out), .in3(bit_extender_1_out),
    .in4(xor_1_out), .in5(shifter_2_out), .in6(or_1_out), .in7(and_1_out), .in8(multiplier_1_out),
    .in9(multiplier_1_cout), .in11(mulh_1_lower), .in12(subtractor_1_out), .in13(shifter_3_out), .in15(B),
    .out(Result), .sel(ALUsel));  // open: in10, in14, en
  assign bit_extender_3_out = {{28{1'b0}}, 4'b0000};  // Bit_Extender bit_extender_3
  Comparator #(.width(32)) comparator_3 (.a(Result), .b(bit_extender_3_out), .eq(is_zero));  // open: gt, lt
  Comparator #(.width(4)) comparator_4 (.a(ALUsel), .b(4'b0000), .eq(comparator_4_eq));  // open: gt, lt
  and and_2 (Overflow, big_adder_1_overflow, comparator_4_eq);

  // Notes on the sheet:
  //   Adder
endmodule

module big_adder (
  input  [31:0] A,
  input  [31:0] B,
  output [31:0] out_3,
  output Overflow,
  output COUT
);

  wire adder_1_cout;

  Adder #(.width(31)) adder_1 (.a(A[30:0]), .b(B[30:0]), .out(out_3[30:0]), .cout(adder_1_cout));  // open: cin
  Adder #(.width(1)) adder_2 (.a(A[31]), .b(B[31]), .out(out_3[31]), .cin(adder_1_cout), .cout(COUT));
  xor xor_1 (Overflow, adder_1_cout, COUT);
endmodule

module MULh (
  input  [31:0] NUM1,
  input  in_2,
  input  [31:0] NUM2,
  output [31:0] LOWER,
  output [31:0] HIgher
);

  wire [31:0] mulh_adder_1_higher, mulh_adder_1_lower, mulh_adder_2_higher, mulh_adder_2_lower,
       mulh_adder_3_higher, mulh_adder_3_lower, mulh_adder_4_higher, mulh_adder_4_lower, mulh_adder_5_higher,
       mulh_adder_5_lower, mulh_adder_6_higher, mulh_adder_6_lower, MULhadder_higher, MULhadder_lower,
       multiplier_1_cout, multiplier_1_out, multiplier_2_cout, multiplier_2_out, multiplier_3_cout,
       multiplier_3_out, multiplier_4_cout, multiplier_4_out, multiplier_5_cout, multiplier_5_out,
       multiplier_6_cout, multiplier_6_out, multiplier_7_cout, multiplier_7_out, multiplier_8_cout,
       multiplier_8_out, multiplier_9_cout, multiplier_9_out;

  Multiplier #(.width(32)) multiplier_1 (
    .a({in_2, NUM1[31], {30{in_2}}}), .b({in_2, NUM2[31], {30{in_2}}}), .out(multiplier_1_out),
    .cout(multiplier_1_cout));  // open: cin
  Multiplier #(.width(32)) multiplier_2 (
    .a({in_2, NUM1[31], {30{in_2}}}), .b({in_2, NUM2[31], {30{in_2}}}), .out(multiplier_2_out),
    .cout(multiplier_2_cout));  // open: cin
  Multiplier #(.width(32)) multiplier_3 (
    .a({in_2, NUM1[31], {30{in_2}}}), .b({in_2, NUM2[31], {30{in_2}}}), .out(multiplier_3_out),
    .cout(multiplier_3_cout));  // open: cin
  Multiplier #(.width(32)) multiplier_4 (
    .a({in_2, NUM1[31], {30{in_2}}}), .b({in_2, NUM2[31], {30{in_2}}}), .out(multiplier_4_out),
    .cout(multiplier_4_cout));  // open: cin
  Multiplier #(.width(32)) multiplier_5 (
    .a({in_2, NUM1[31], {30{in_2}}}), .b({in_2, NUM2[30:0]}), .out(multiplier_5_out), .cout(multiplier_5_cout));  // open: cin
  Multiplier #(.width(32)) multiplier_6 (
    .a({in_2, NUM1[31], {30{in_2}}}), .b({in_2, NUM2[30:0]}), .out(multiplier_6_out), .cout(multiplier_6_cout));  // open: cin
  Multiplier #(.width(32)) multiplier_7 (
    .a({in_2, NUM1[30:0]}), .b({in_2, NUM2[31], {30{in_2}}}), .out(multiplier_7_out), .cout(multiplier_7_cout));  // open: cin
  Multiplier #(.width(32)) multiplier_8 (
    .a({in_2, NUM1[30:0]}), .b({in_2, NUM2[31], {30{in_2}}}), .out(multiplier_8_out), .cout(multiplier_8_cout));  // open: cin
  Multiplier #(.width(32)) multiplier_9 (
    .a({in_2, NUM1[30:0]}), .b({in_2, NUM2[30:0]}), .out(multiplier_9_out), .cout(multiplier_9_cout));  // open: cin
  MULH_adder mulh_adder_1 (
    .L_1_LOWER_cb844c56(multiplier_1_out), .L_1_HIGHER_e69bc68c(multiplier_1_cout),
    .L_2_LOWER_60b3a6f1(multiplier_2_out), .L_2_HIGHER_1b9c1836(multiplier_2_cout),
    .LOwer(mulh_adder_1_lower), .higher(mulh_adder_1_higher));
  MULH_adder MULhadder (
    .L_1_LOWER_cb844c56(multiplier_3_out), .L_1_HIGHER_e69bc68c(multiplier_3_cout),
    .L_2_LOWER_60b3a6f1(multiplier_4_out), .L_2_HIGHER_1b9c1836(multiplier_4_cout), .LOwer(MULhadder_lower),
    .higher(MULhadder_higher));
  MULH_adder mulh_adder_2 (
    .L_1_LOWER_cb844c56(multiplier_5_out), .L_1_HIGHER_e69bc68c(multiplier_5_cout),
    .L_2_LOWER_60b3a6f1(multiplier_6_out), .L_2_HIGHER_1b9c1836(multiplier_6_cout),
    .LOwer(mulh_adder_2_lower), .higher(mulh_adder_2_higher));
  MULH_adder mulh_adder_3 (
    .L_1_LOWER_cb844c56(multiplier_7_out), .L_1_HIGHER_e69bc68c(multiplier_7_cout),
    .L_2_LOWER_60b3a6f1(multiplier_8_out), .L_2_HIGHER_1b9c1836(multiplier_8_cout),
    .LOwer(mulh_adder_3_lower), .higher(mulh_adder_3_higher));
  MULH_adder mulh_adder_4 (
    .L_1_LOWER_cb844c56(mulh_adder_1_lower), .L_1_HIGHER_e69bc68c(mulh_adder_1_higher),
    .L_2_LOWER_60b3a6f1(MULhadder_lower), .L_2_HIGHER_1b9c1836(MULhadder_higher), .LOwer(mulh_adder_4_lower),
    .higher(mulh_adder_4_higher));
  MULH_adder mulh_adder_5 (
    .L_1_LOWER_cb844c56(mulh_adder_2_lower), .L_1_HIGHER_e69bc68c(mulh_adder_2_higher),
    .L_2_LOWER_60b3a6f1(mulh_adder_3_lower), .L_2_HIGHER_1b9c1836(mulh_adder_3_higher),
    .LOwer(mulh_adder_5_lower), .higher(mulh_adder_5_higher));
  MULH_adder mulh_adder_6 (
    .L_1_LOWER_cb844c56(mulh_adder_4_lower), .L_1_HIGHER_e69bc68c(mulh_adder_4_higher),
    .L_2_LOWER_60b3a6f1(mulh_adder_5_lower), .L_2_HIGHER_1b9c1836(mulh_adder_5_higher),
    .LOwer(mulh_adder_6_lower), .higher(mulh_adder_6_higher));
  MULH_adder mulh_adder_7 (
    .L_1_LOWER_cb844c56(mulh_adder_6_lower), .L_1_HIGHER_e69bc68c(mulh_adder_6_higher),
    .L_2_LOWER_60b3a6f1(multiplier_9_out), .L_2_HIGHER_1b9c1836(multiplier_9_cout), .LOwer(LOWER),
    .higher(HIgher));
endmodule

module MULH_adder (
  input  [31:0] L_1_LOWER_cb844c56,
  input  [31:0] L_1_HIGHER_e69bc68c,
  input  [31:0] L_2_LOWER_60b3a6f1,
  input  [31:0] L_2_HIGHER_1b9c1836,
  output [31:0] LOwer,
  output [31:0] higher
);

  wire adder_1_cout;

  Adder #(.width(32)) adder_1 (
    .a(L_1_LOWER_cb844c56), .b(L_2_LOWER_60b3a6f1), .out(LOwer), .cout(adder_1_cout));  // open: cin
  Adder #(.width(32)) adder_2 (
    .a(L_1_HIGHER_e69bc68c), .b(L_2_HIGHER_1b9c1836), .out(higher), .cin(adder_1_cout));  // open: cout
endmodule
