// Logisim project Processor.circ as structural Verilog: 2 circuits, main circuit decode
module decode (
  input  [31:0] Instructions,
  output beq_indicator,
  output Redmem,
  output [4:0] writeidx,
  output Writemem,
  output Write,
  output [4:0] r1_idx,
  output [4:0] r2_idx,
  output ALUsrc,
  output [31:0] immediate,
  output [3:0] Aluop
);

  wire comparator_2_eq, comparator_3_eq, or_3_out;
  wire [3:0] alusel_1_i_type, multiplexer_3_out;
  wire [31:0] bit_extender_1_out, bit_extender_2_out, bit_extender_3_out, multiplexer_1_out;

  Comparator comparator_1 (.a({1'b0, Instructions[6:0]}), .b(8'h3), .eq(Redmem));  // open: gt, lt
  Comparator comparator_2 (.a({1'b0, Instructions[6:0]}), .b(8'h33), .eq(comparator_2_eq));  // open: gt, lt
  Comparator comparator_3 (.a({1'b0, Instructions[6:0]}), .b(8'h13), .eq(comparator_3_eq));  // open: gt, lt
  or or_1 (Write, Redmem, comparator_2_eq, comparator_3_eq);
  assign bit_extender_1_out = {{20{Instructions[31]}}, Instructions[31:20]};  // Bit_Extender bit_extender_1
  Comparator comparator_4 (.a({1'b0, Instructions[6:0]}), .b(8'h23), .eq(Writemem));  // open: gt, lt
  assign bit_extender_2_out = {{20{Instructions[31]}}, {Instructions[31:25], Instructions[11:7]}};  // Bit_Extender bit_extender_2
  assign bit_extender_3_out = {{21{Instructions[31]}}, {Instructions[31], Instructions[7], Instructions[30:25], Instructions[11:9]}};  // Bit_Extender bit_extender_3
  Comparator comparator_5 (.a({1'b0, Instructions[6:0]}), .b(8'h63), .eq(beq_indicator));  // open: gt, lt
  Multiplexer #(.width(32)) multiplexer_1 (
    .in0(bit_extender_1_out), .in1(bit_extender_2_out), .out(multiplexer_1_out), .sel(Writemem));
  or or_2 (ALUsrc, comparator_3_eq, Writemem);
  Multiplexer #(.width(32)) multiplexer_2 (
    .in0(multiplexer_1_out), .in1(bit_extender_3_out), .out(immediate), .sel(beq_indicator));
  alusel alusel_1 (.i_type(alusel_1_i_type));  // open: Rinput, RIselector, I_input, r_type, ALUSel
  Multiplexer #(.width(4)) multiplexer_3 (
    .in0(alusel_1_i_type), .in1(4'b1100), .out(multiplexer_3_out), .sel(beq_indicator));
  or or_3 (or_3_out, Writemem, Redmem);
  Multiplexer #(.width(4)) multiplexer_4 (.in0(multiplexer_3_out), .in1(4'b0000), .out(Aluop), .sel(or_3_out));

  assign r1_idx = Instructions[19:15];
  assign r2_idx = Instructions[24:20];
  assign writeidx = Instructions[11:7];

  // Notes on the sheet:
  //   immdiate
  //   swimmediate
  //   beq
endmodule

module proceesor_circuit (
  input  Clear1,
  input  Clear2,
  input  ZERo,
  input  PC_resetter,
  input  in_5,
  input  in_6,
  output Branched,
  output [31:0] out_8,
  output [31:0] WriteDATAAA,
  output [4:0] WRITEREGISTER
);

  wire alucircuit_1_overflow, clock_1_out, decode_1_alusrc, decode_1_beq_indicator, decode_1_redmem,
       decode_1_write, decode_1_writemem;
  wire [3:0] decode_1_aluop;
  wire [4:0] decode_1_r1_idx, decode_1_r2_idx;
  wire [23:0] alucircuit_1_result;
  wire [31:0] adder_1_out, decode_1_immediate, multiplexer_1_out, multiplexer_2_out, ram_2_dout,
       register_1_q, registerfile_1_readdata1, registerfile_1_readdata2;
  wire [31:24] alucircuit_1_result_2;

  Clock clock_1 (.out(clock_1_out));
  Register #(.width(32)) register_1 (
    .D(adder_1_out), .en(1'b1), .clk(clock_1_out), .Q(register_1_q), .clr(PC_resetter));
  RAM #(.addrWidth(24), .dataWidth(32)) ram_1 (
    .addr(register_1_q[23:0]), .we(in_5), .oe(in_6), .clk(clock_1_out), .din({32{1'b0}}), .dout(out_8));
  Adder #(.width(32)) adder_1 (.a(multiplexer_1_out), .b(register_1_q), .out(adder_1_out));  // open: cin, cout
  decode decode_1 (
    .Instructions(out_8), .beq_indicator(decode_1_beq_indicator), .Redmem(decode_1_redmem),
    .writeidx(WRITEREGISTER), .Writemem(decode_1_writemem), .Write(decode_1_write), .r1_idx(decode_1_r1_idx),
    .r2_idx(decode_1_r2_idx), .ALUsrc(decode_1_alusrc), .immediate(decode_1_immediate), .Aluop(decode_1_aluop));
  Multiplexer #(.width(32)) multiplexer_1 (
    .in0(32'h1), .in1(decode_1_immediate), .out(multiplexer_1_out), .sel(Branched));
  Registerfile registerfile_1 (
    .Zero(ZERo), .Clear1(Clear1), .Clear2(Clear2), .RegWEn(decode_1_write), .clock(clock_1_out),
    .ReadRegister1(decode_1_r1_idx), .ReadRegister2(decode_1_r2_idx), .Write_Data(WriteDATAAA),
    .Write_Register1(WRITEREGISTER), .ReadData1(registerfile_1_readdata1),
    .ReadData2(registerfile_1_readdata2));
  Multiplexer #(.width(32)) multiplexer_2 (
    .in0(registerfile_1_readdata2), .in1(decode_1_immediate), .out(multiplexer_2_out), .sel(decode_1_alusrc));
  and and_1 (Branched, decode_1_beq_indicator, alucircuit_1_overflow);
  ALUcircuit alucircuit_1 (
    .Result({alucircuit_1_result_2, alucircuit_1_result}), .Overflow(alucircuit_1_overflow));  // open: ALUsel, A, B, is_zero
  RAM #(.addrWidth(24), .dataWidth(32)) ram_2 (
    .addr(alucircuit_1_result), .we(decode_1_writemem), .oe(decode_1_redmem), .clk(clock_1_out),
    .din(registerfile_1_readdata2), .dout(ram_2_dout));
  Multiplexer #(.width(32)) multiplexer_3 (
    .in0({alucircuit_1_result_2, alucircuit_1_result}), .in1(ram_2_dout), .out(WriteDATAAA),
    .sel(decode_1_redmem));
endmodule
