// Logisim project aluselector.circ as structural Verilog: 1 circuit, main circuit alusel
module alusel (
  input  [3:0] Rinput,
  input  RIselector,
  input  [2:0] I_input,
  output [3:0] r_type,
  output [3:0] ALUSel,
  output [3:0] i_type
);

  Multiplexer #(.enable("true"), .select(4), .width(4)) multiplexer_1 (
    .in0(4'b0000), .in1(4'b0001), .in2(4'b0010), .in3(4'b0011), .in4(4'b0100), .in5(4'b0101), .in6(4'b0110),
    .in7(4'b0111), .in8(4'b1100), .out(r_type), .sel(Rinput));  // open: in9, in10, in11, in12, in13, in14, in15, en
  Multiplexer #(.enable("true"), .select(3), .width(4)) multiplexer_2 (
    .in0(4'b0000), .in1(4'b0001), .in2(4'b0010), .in3(4'b0011), .in4(4'b0100), .in5(4'b0101), .in6(4'b0110),
    .in7(4'b0111), .out(i_type), .sel(I_input));  // open: en
  Multiplexer #(.enable("true"), .width(4)) multiplexer_3 (
    .in0(r_type), .in1(i_type), .out(ALUSel), .sel(RIselector));  // open: en
endmodule
