// Logisim project register.circ as structural Verilog: 2 circuits, main circuit registers
module Registerfile (
  input  Zero,
  input  Clear1,
  input  Clear2,
  input  RegWEn,
  input  clock,
  input  [4:0] ReadRegister1,
  input  [4:0] ReadRegister2,
  input  [31:0] Write_Data,
  input  [4:0] Write_Register1,
  output [31:0] ReadData1,
  output [31:0] ReadData2
);

  wire and_1_out, and_2_out, and_3_out, and_4_out, and_5_out, and_6_out, and_7_out, and_8_out,
       decoder_1_out1, decoder_1_out2, decoder_1_out5, decoder_1_out6, decoder_1_out7, decoder_1_out8,
       decoder_1_out9, decoder_1_out10;
  wire [31:0] registers_1_output, registers_2_output, registers_3_output, registers_4_output,
       registers_5_output, registers_6_output, registers_7_output, registers_8_output, registers_9_output;

  Decoder #(.select(5)) decoder_1 (
    .out1(decoder_1_out1), .out2(decoder_1_out2), .out5(decoder_1_out5), .out6(decoder_1_out6),
    .out7(decoder_1_out7), .out8(decoder_1_out8), .out9(decoder_1_out9), .out10(decoder_1_out10),
    .sel(Write_Register1));  // open: out0, out3, out4, out11, out12, out13, out14, out15, out16, out17, out18, out19, out20, out21, out22, out23, out24, out25, out26, out27, out28, out29, out30, out31, en
  registers registers_1 (.Input({32{1'b0}}), .enable(1'b0), .clock(clock), .clear(Zero), .\output (registers_1_output));
  registers registers_2 (
    .Input(Write_Data), .enable(and_1_out), .clock(clock), .clear(Clear1), .\output (registers_2_output));
  and and_1 (and_1_out, RegWEn, decoder_1_out1);
  registers registers_3 (
    .Input(Write_Data), .enable(and_2_out), .clock(clock), .clear(Clear1), .\output (registers_3_output));
  and and_2 (and_2_out, RegWEn, decoder_1_out2);
  registers registers_4 (
    .Input(Write_Data), .enable(and_3_out), .clock(clock), .clear(Clear1), .\output (registers_4_output));
  and and_3 (and_3_out, RegWEn, decoder_1_out5);
  and and_4 (and_4_out, RegWEn, decoder_1_out6);
  registers registers_5 (
    .Input(Write_Data), .enable(and_4_out), .clock(clock), .clear(Clear1), .\output (registers_5_output));
  and and_5 (and_5_out, RegWEn, decoder_1_out7);
  registers registers_6 (
    .Input(Write_Data), .enable(and_5_out), .clock(clock), .clear(Clear2), .\output (registers_6_output));
  and and_6 (and_6_out, RegWEn, decoder_1_out8);
  and and_7 (and_7_out, decoder_1_out9, RegWEn);
  and and_8 (and_8_out, decoder_1_out10, RegWEn);
  registers registers_7 (
    .Input(Write_Data), .enable(and_6_out), .clock(clock), .clear(Clear2), .\output (registers_7_output));
  registers registers_8 (
    .Input(Write_Data), .enable(and_7_out), .clock(clock), .clear(Clear2), .\output (registers_8_output));
  registers registers_9 (
    .Input(Write_Data), .enable(and_8_out), .clock(clock), .clear(Clear2), .\output (registers_9_output));
  Multiplexer #(.enable("true"), .select(5), .width(32)) multiplexer_1 (
    .in0(registers_1_output), .in1(registers_2_output), .in2(registers_3_output), .in5(registers_4_output),
    .in6(registers_5_output), .in7(registers_6_output), .in8(registers_7_output), .in9(registers_8_output),
    .in10(registers_9_output), .out(ReadData1), .sel(ReadRegister1));  // open: in3, in4, in11, in12, in13, in14, in15, in16, in17, in18, in19, in20, in21, in22, in23, in24, in25, in26, in27, in28, in29, in30, in31, en
  Multiplexer #(.enable("true"), .select(5), .width(32)) multiplexer_2 (
    .in0(registers_1_output), .in1(registers_2_output), .in2(registers_3_output), .in5(registers_4_output),
    .in6(registers_5_output), .in7(registers_6_output), .in8(registers_7_output), .in9(registers_9_output),
    .out(ReadData2), .sel(ReadRegister2));  // open: in3, in4, in10, in11, in12, in13, in14, in15, in16, in17, in18, in19, in20, in21, in22, in23, in24, in25, in26, in27, in28, in29, in30, in31, en
endmodule

module registers (
  input  [31:0] Input,
  input  enable,
  input  clock,
  input  clear,
  output [31:0] \output 
);

  Register #(.width(32)) register_1 (.D(Input), .en(enable), .clk(clock), .Q(\output ), .clr(clear));
endmodule
